# Fritzing sketch v1 (saved by Fritzing 1.0.1rc)
breadboards: 1

parts:
  Q1 = NPN-Transistor [package="TO92 [THT]"]
  D1 = Diode [package=diode-1n4001]
  JP1 = Header 2 [package=jst-2-pth]
  R1 = Resistor [tolerance=±5% resistance=1k package="0805 [SMD]"]
  C2 = Electrolytic Capacitor [capacitance=1μF voltage=35V package="0405 [SMD, electrolytic]"]
  U2 = ESP32-38PinWide [part_number=ESP32-38PinWide]
  R3 = Resistor [tolerance=±5% resistance=100 package="1206 [SMD]"]
  C1 = Capacitor [package=cap-pth-small]
  C3 = Capacitor [package=cap-pth-small]
  C5 = Capacitor [package=cap-pth-small]
  M1 = Grove GSR Sensor
  SparkFun_LiPo_Charger_Basic_-_Micro-USB1 = SparkFun LiPo Charger Basic - Micro-USB [part_number=PRT-10217]
  Pololu_U3V70F1 = Pololu Step-up voltage regulator U3V70F5 [part_number=? package=?]
  R4 = Resistor [tolerance=±5% resistance=220 package="0603 [SMD]"]
  R6 = Resistor [tolerance=±5% resistance=220 package="0603 [SMD]"]
  R7 = Resistor [tolerance=±5% resistance=220 package="0603 [SMD]"]
  LED2 = smd LED [color="Red (633nm)" package="0603 [SMD]"]
  LED1 = smd LED [color="Yellow (595nm)" package="0603 [SMD]"]
  LED3 = smd LED [color="Green (565nm)" package="0603 [SMD]"]
  U3 = SWITCH_SPDT [package=kps-1290]

nets:
  N1: Q1.E, C2.-, U2.GPIO11, C1.2, C3.1, M1.GND, Pololu_U3V70F1.GND#2, LED2.cathode, LED1.cathode
  N2: Q1.B, R1.Pin_1
  N3: Q1.C, D1.A, JP1.2
  N4: D1.C, JP1.1, C2.+, U2.VIN, C1.1, U3.O
  N5: R1.Pin_0, U2.GPIO25
  N6: U2.3.3, C3.2, C5.1, M1.VCC
  N7: U2.GPIO32, R3.Pin_0, C5.2
  N8: U2.GPIO27, R6.Pin_1
  N9: U2.GPIO14, R4.Pin_1
  N10: U2.GPIO12, R7.Pin_1
  N11: R3.Pin_1, M1.SIG
  N12: SparkFun_LiPo_Charger_Basic_-_Micro-USB1.GND, Pololu_U3V70F1.GND#7
  VCC: SparkFun_LiPo_Charger_Basic_-_Micro-USB1.VCC, Pololu_U3V70F1.VIN
  N13: Pololu_U3V70F1.VOUT, U3.P
  N14: R4.Pin_0, LED2.anode
  N15: R6.Pin_0, LED1.anode
  N16: R7.Pin_0, LED3.anode

notes:
  5v line
  step up polulu 5V
  Lipo charger basic microusb
  3v3 line
  pump connector
  diode skotchy transistor bc 337-16
  capacitors: 100uf ceramic; 470 uf electrolitic
  Groove GSR sensor
  https://wiki.seeedstudio.com/Grove-GSR_Sensor/
  optional resistor: R from base to GND (100k)
  USEFUL INDICATIONS:
  1) GND sensor & GND pump in one point near ESP's GND.
  2) check the calculation for Rb value (pwm)
  3) capacitor needs to stay as closer as possible to the gpio32, gnd & Vcc common points
  31/10:
  for now all is usb powered
  5/11: 5V supply addedd
  DEBUG LED
  LED1 (Y) PIN 27
  LED2 (R) PIN 14
  LED3 (G) PIN 12

custom parts:
  ESP32-38PinWide: Generic 38-Pin ESP32 with wide format (only access to one side of pins on a breadboard) based on Stephen Lilley's HiLetgo ESP-WROOM-32 ESP32 ESP-32S Development Board.
  Grove GSR Sensor: GSR stands for galvanic skin response, is a method of measuring the electrical conductance of the skin. Strong emotion can cause stimulus to your sympathetic nervous system, resulting more sweat being secreted by the sweat glands.
  SparkFun LiPo Charger Basic - Micro-USB: Description: If you need to charge LiPo batteries, this simple charger will do just that, and do it fast! The SparkFun LiPo Charger Basic is stripped down of all features and just does one thing well - charge 3.7V LiPo cells at a rate of 500mA. It is designed to charge single-cell Li-Ion or Li-Polymer batteries. Check the datasheet below to see if it will work with your battery. The board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
  Pololu Step-up voltage regulator U3V70F5: Step-Up voltage regulator.
